# Fritzing sketch schemat (saved by Fritzing 0.9.6b)
breadboards: 1

parts:
  Atmega1 = ATmega328 [package=tqfp]
  VCC1 = Battery block 9V
  C1 = Ceramic Capacitor [capacitance="100 nF" voltage=35V package="0603 [SMD, multilayer]"]
  C2 = Ceramic Capacitor [capacitance="100 nF" voltage=35V package="0603 [SMD, multilayer]"]
  Q1 = Basic FET N-Channel [package="TO220 [THT]"]
  LED1 = LED - 3mm [color="Red (633nm)" current=0.030 package="3 mm [THT]"]
  R1 = Resistor [tolerance=±5% resistance=330 package="1206 [SMD]"]
  R2 = Resistor [tolerance=±5% resistance=10k package="1206 [SMD]"]
  C3 = Ceramic Capacitor [capacitance="100 nF" voltage=35V package="0603 [SMD, multilayer]"]
  C4 = Ceramic Capacitor [capacitance="100 nF" voltage=35V package="0603 [SMD, multilayer]"]
  XTAL1 = Crystal [frequency="16 Mhz" package=THT]
  LED2 = LED - 3mm [color="Yellow (595nm)" current=0.030 package="3 mm [THT]"]
  LED3 = LED - 3mm [color="Green (570nm)" current=0.030 package="3 mm [THT]"]
  R3 = Resistor [tolerance=±5% resistance=330 package="1206 [SMD]"]
  R4 = Resistor [tolerance=±5% resistance=330 package="1206 [SMD]"]
  Part1 = Soil Moisture Sensor

nets:
  N1: Atmega1.PD3(INT1), R2.Pin_1
  N2: Atmega1.VCC, LED1.anode
  N3: Atmega1.PB6(XTAL1_TOSC1), Atmega1.PC1(ADC1), VCC1.+, C1.0, C2.0, Q1.drain, Q1.source, R2.Pin_0, C3.0, C4.1, Part1.VCC
  N4: Atmega1.PB7(XTAL2_TOSC2), Atmega1.PC3(ADC3), VCC1.-, C1.1, C2.1, Q1.gate, R1.Pin_0, C3.1, C4.0, R3.Pin_0, R4.Pin_0, Part1.GND
  N5: Atmega1.PD5(T1), XTAL1.pin_1
  N6: Atmega1.PD6(AIN0), XTAL1.pin_0
  N7: Atmega1.PB4(MISO), LED2.anode
  N8: Atmega1.AREF, LED3.anode
  N9: Atmega1.PD2(INT0), Part1.SIG
  N10: LED1.cathode, R1.Pin_1
  N11: LED2.cathode, R3.Pin_1
  N12: LED3.cathode, R4.Pin_1
