# Fritzing sketch schemat_pcb (saved by Fritzing 0.9.3b)
perfboards: 1

parts:
  Q2 = Basic FET N-Channel [package="TO220 [THT]"]  # not connected
  VCC2 = Battery block 9V
  R3 = Resistor [tolerance=±5% resistance=10k package="1206 [SMD]"]
  XTAL2 = Crystal [frequency="16 Mhz" package=THT]
  C7 = Ceramic Capacitor [capacitance="100 nF" voltage=35V package="0603 [SMD, multilayer]"]
  C8 = Ceramic Capacitor [capacitance="100 nF" voltage=35V package="0603 [SMD, multilayer]"]  # not connected
  C9 = Ceramic Capacitor [capacitance="100 nF" voltage=35V package="0603 [SMD, multilayer]"]  # not connected
  C10 = Ceramic Capacitor [capacitance="100 nF" voltage=35V package="0603 [SMD, multilayer]"]  # not connected
  LED2 = LED - 3mm [color="Red (633nm)" current=0.030 package="3 mm [THT]"]
  LED3 = LED - 3mm [color="Yellow (595nm)" current=0.030 package="3 mm [THT]"]
  LED4 = LED - 3mm [color="Green (570nm)" current=0.030 package="3 mm [THT]"]
  R4 = Resistor [tolerance=±5% resistance=330 package="1206 [SMD]"]
  R5 = Resistor [tolerance=±5% resistance=330 package="1206 [SMD]"]
  R6 = Resistor [tolerance=±5% resistance=330 package="1206 [SMD]"]
  Part2 = Soil Moisture Sensor
  Atmega1 = atmega328 [package=dip]

nets:
  N1: VCC2.-, Part2.GND
  N2: VCC2.+, Part2.VCC
  N3: R3.Pin_1, Atmega1.RESET
  N4: XTAL2.pin_0, Atmega1.XLAT2
  N5: XTAL2.pin_1, Atmega1.XLAT1
  N6: C7.0, Atmega1.GND#7
  N7: C7.1, Atmega1.VCC
  N8: LED2.cathode, R4.Pin_1
  N9: LED2.anode, Atmega1.D2
  N10: LED3.cathode, R5.Pin_1
  N11: LED3.anode, Atmega1.D8
  N12: LED4.cathode, R6.Pin_1
  N13: LED4.anode, Atmega1.D12
  N14: Part2.SIG, Atmega1.A5
